// Logisim project 24HRCLOCK.circ as structural Verilog: 6 circuits, main circuit main
module main (
  input  SET_MINUTE,
  input  SET_SECONDS,
  input  SET_HOUR,
  input  STOP
);

  wire and_1_out, clock_1_out, decade_1_q0, decade_1_q1, decade_1_q2, decade_1_q3, decade_2_q0, decade_2_q1,
       decade_2_q2, decade_2_q3, decade_3_q0, decade_3_q1, decade_3_q2, decade_3_q3, mod3_1_q0, mod3_1_q1,
       mod6_1_q0, mod6_1_q1, mod6_1_q2, mod6_2_q0, mod6_2_q1, mod6_2_q2, n7_seg_driver_1_a,
       n7_seg_driver_1_b, n7_seg_driver_1_c, n7_seg_driver_1_d, n7_seg_driver_1_e, n7_seg_driver_1_f,
       n7_seg_driver_1_g, n7_seg_driver_2_a, n7_seg_driver_2_b, n7_seg_driver_2_c, n7_seg_driver_2_d,
       n7_seg_driver_2_e, n7_seg_driver_2_f, n7_seg_driver_2_g, n7_seg_driver_2_nxt, n7_seg_driver_3_a,
       n7_seg_driver_3_b, n7_seg_driver_3_c, n7_seg_driver_3_d, n7_seg_driver_3_e, n7_seg_driver_3_f,
       n7_seg_driver_3_g, n7_seg_driver_3_nxt, n7_seg_driver_4_a, n7_seg_driver_4_b, n7_seg_driver_4_c,
       n7_seg_driver_4_d, n7_seg_driver_4_e, n7_seg_driver_4_f, n7_seg_driver_4_g, n7_seg_driver_4_nxt,
       n7_seg_driver_mod6_1_a, n7_seg_driver_mod6_1_b, n7_seg_driver_mod6_1_c, n7_seg_driver_mod6_1_d,
       n7_seg_driver_mod6_1_e, n7_seg_driver_mod6_1_f, n7_seg_driver_mod6_1_g, n7_seg_driver_mod6_1_nxt,
       n7_seg_driver_mod6_2_a, n7_seg_driver_mod6_2_b, n7_seg_driver_mod6_2_c, n7_seg_driver_mod6_2_d,
       n7_seg_driver_mod6_2_e, n7_seg_driver_mod6_2_f, n7_seg_driver_mod6_2_g, n7_seg_driver_mod6_2_nxt,
       nand_1_out, not_1_out, or_1_out, xor_1_out, xor_2_out;

  Clock clock_1 (.out(clock_1_out));
  not not_1 (not_1_out, STOP);
  and and_1 (and_1_out, clock_1_out, not_1_out);
  mod3 mod3_1 (.CLK(n7_seg_driver_2_nxt), .CLR(nand_1_out), .VCC(1'b1), .Q0(mod3_1_q0), .Q1(mod3_1_q1));
  nand nand_1 (nand_1_out, mod3_1_q1, decade_1_q2);
  _7_seg_driver u_7_seg_driver_1 (
    .EN_prime(1'b0), .Q0(mod3_1_q0), .Q1(mod3_1_q1), .Q2(1'b0), .Q3(1'b0), .A(n7_seg_driver_1_a),
    .B(n7_seg_driver_1_b), .C(n7_seg_driver_1_c), .D(n7_seg_driver_1_d), .E(n7_seg_driver_1_e),
    .F(n7_seg_driver_1_f), .G(n7_seg_driver_1_g));  // open: NXT
  _7_Segment_Display u_7_segment_display_1 (
    .g(n7_seg_driver_1_g), .f(n7_seg_driver_1_f), .a(n7_seg_driver_1_a), .b(n7_seg_driver_1_b),
    .e(n7_seg_driver_1_e), .d(n7_seg_driver_1_d), .c(n7_seg_driver_1_c));  // open: dp
  decade decade_1 (
    .CLR(nand_1_out), .CLK(xor_1_out), .VCC(1'b1), .Q0(decade_1_q0), .Q1(decade_1_q1), .Q2(decade_1_q2),
    .Q3(decade_1_q3));
  _7_seg_driver u_7_seg_driver_2 (
    .EN_prime(1'b0), .Q0(decade_1_q0), .Q1(decade_1_q1), .Q2(decade_1_q2), .Q3(decade_1_q3),
    .NXT(n7_seg_driver_2_nxt), .A(n7_seg_driver_2_a), .B(n7_seg_driver_2_b), .C(n7_seg_driver_2_c),
    .D(n7_seg_driver_2_d), .E(n7_seg_driver_2_e), .F(n7_seg_driver_2_f), .G(n7_seg_driver_2_g));
  _7_Segment_Display u_7_segment_display_2 (
    .g(n7_seg_driver_2_g), .f(n7_seg_driver_2_f), .a(n7_seg_driver_2_a), .b(n7_seg_driver_2_b),
    .e(n7_seg_driver_2_e), .d(n7_seg_driver_2_d), .c(n7_seg_driver_2_c));  // open: dp
  LED led_1 (.in(and_1_out));
  LED led_2 (.in(and_1_out));
  xor xor_1 (xor_1_out, SET_HOUR, n7_seg_driver_mod6_1_nxt);
  mod6 mod6_1 (.CLK(n7_seg_driver_3_nxt), .CLR(nand_1_out), .VCC(1'b1), .Q0(mod6_1_q0), .Q1(mod6_1_q1), .Q2(mod6_1_q2));
  _7_seg_driver_mod6 u_7_seg_driver_mod6_1 (
    .EN_prime(1'b0), .Q0(mod6_1_q0), .Q1(mod6_1_q1), .Q2(mod6_1_q2), .Q3(1'b0),
    .NXT(n7_seg_driver_mod6_1_nxt), .A(n7_seg_driver_mod6_1_a), .B(n7_seg_driver_mod6_1_b),
    .C(n7_seg_driver_mod6_1_c), .D(n7_seg_driver_mod6_1_d), .E(n7_seg_driver_mod6_1_e),
    .F(n7_seg_driver_mod6_1_f), .G(n7_seg_driver_mod6_1_g));
  _7_Segment_Display u_7_segment_display_3 (
    .g(n7_seg_driver_mod6_1_g), .f(n7_seg_driver_mod6_1_f), .a(n7_seg_driver_mod6_1_a),
    .b(n7_seg_driver_mod6_1_b), .e(n7_seg_driver_mod6_1_e), .d(n7_seg_driver_mod6_1_d),
    .c(n7_seg_driver_mod6_1_c));  // open: dp
  decade decade_2 (
    .CLR(nand_1_out), .CLK(xor_2_out), .VCC(1'b1), .Q0(decade_2_q0), .Q1(decade_2_q1), .Q2(decade_2_q2),
    .Q3(decade_2_q3));
  _7_seg_driver u_7_seg_driver_3 (
    .EN_prime(1'b0), .Q0(decade_2_q0), .Q1(decade_2_q1), .Q2(decade_2_q2), .Q3(decade_2_q3),
    .NXT(n7_seg_driver_3_nxt), .A(n7_seg_driver_3_a), .B(n7_seg_driver_3_b), .C(n7_seg_driver_3_c),
    .D(n7_seg_driver_3_d), .E(n7_seg_driver_3_e), .F(n7_seg_driver_3_f), .G(n7_seg_driver_3_g));
  _7_Segment_Display u_7_segment_display_4 (
    .g(n7_seg_driver_3_g), .f(n7_seg_driver_3_f), .a(n7_seg_driver_3_a), .b(n7_seg_driver_3_b),
    .e(n7_seg_driver_3_e), .d(n7_seg_driver_3_d), .c(n7_seg_driver_3_c));  // open: dp
  xor xor_2 (xor_2_out, SET_MINUTE, n7_seg_driver_mod6_2_nxt);
  mod6 mod6_2 (.CLK(n7_seg_driver_4_nxt), .CLR(nand_1_out), .VCC(1'b1), .Q0(mod6_2_q0), .Q1(mod6_2_q1), .Q2(mod6_2_q2));
  LED led_3 (.in(and_1_out));
  LED led_4 (.in(and_1_out));
  _7_seg_driver_mod6 u_7_seg_driver_mod6_2 (
    .EN_prime(1'b0), .Q0(mod6_2_q0), .Q1(mod6_2_q1), .Q2(mod6_2_q2), .Q3(1'b0),
    .NXT(n7_seg_driver_mod6_2_nxt), .A(n7_seg_driver_mod6_2_a), .B(n7_seg_driver_mod6_2_b),
    .C(n7_seg_driver_mod6_2_c), .D(n7_seg_driver_mod6_2_d), .E(n7_seg_driver_mod6_2_e),
    .F(n7_seg_driver_mod6_2_f), .G(n7_seg_driver_mod6_2_g));
  _7_Segment_Display u_7_segment_display_5 (
    .g(n7_seg_driver_mod6_2_g), .f(n7_seg_driver_mod6_2_f), .a(n7_seg_driver_mod6_2_a),
    .b(n7_seg_driver_mod6_2_b), .e(n7_seg_driver_mod6_2_e), .d(n7_seg_driver_mod6_2_d),
    .c(n7_seg_driver_mod6_2_c));  // open: dp
  decade decade_3 (
    .CLR(nand_1_out), .CLK(or_1_out), .VCC(1'b1), .Q0(decade_3_q0), .Q1(decade_3_q1), .Q2(decade_3_q2),
    .Q3(decade_3_q3));
  or or_1 (or_1_out, SET_SECONDS, and_1_out);
  _7_seg_driver u_7_seg_driver_4 (
    .EN_prime(1'b0), .Q0(decade_3_q0), .Q1(decade_3_q1), .Q2(decade_3_q2), .Q3(decade_3_q3),
    .NXT(n7_seg_driver_4_nxt), .A(n7_seg_driver_4_a), .B(n7_seg_driver_4_b), .C(n7_seg_driver_4_c),
    .D(n7_seg_driver_4_d), .E(n7_seg_driver_4_e), .F(n7_seg_driver_4_f), .G(n7_seg_driver_4_g));
  _7_Segment_Display u_7_segment_display_6 (
    .g(n7_seg_driver_4_g), .f(n7_seg_driver_4_f), .a(n7_seg_driver_4_a), .b(n7_seg_driver_4_b),
    .e(n7_seg_driver_4_e), .d(n7_seg_driver_4_d), .c(n7_seg_driver_4_c));  // open: dp

  // Notes on the sheet:
  //   HOURS
  //   24-HOUR DIGITAL CLOCK BY HANNAH BOADIWAA LORMENYO
  //   MINUTES
  //   SECONDS
endmodule

module decade (
  input  VCC,
  input  CLR,
  input  CLK,
  output Q0,
  output Q1,
  output Q2,
  output Q3
);

  wire and_1_out, and_2_out, and_3_out, and_4_out, j_k_ff_4_qn, not_1_out, or_1_out;

  not not_1 (not_1_out, CLR);
  J_K_Flip_Flop j_k_ff_1 (.J(VCC), .clk(CLK), .K(VCC), .Q(Q0), .reset(not_1_out));  // open: Qn, preset, en
  and and_1 (and_1_out, Q0, j_k_ff_4_qn);
  J_K_Flip_Flop j_k_ff_2 (.J(and_1_out), .clk(CLK), .K(and_1_out), .Q(Q1), .reset(not_1_out));  // open: Qn, preset, en
  and and_2 (and_2_out, Q0, Q1);
  J_K_Flip_Flop j_k_ff_3 (.J(and_2_out), .clk(CLK), .K(and_2_out), .Q(Q2), .reset(not_1_out));  // open: Qn, preset, en
  and and_3 (and_3_out, Q3, Q0);
  and and_4 (and_4_out, and_2_out, Q2);
  or or_1 (or_1_out, and_3_out, and_4_out);
  J_K_Flip_Flop j_k_ff_4 (
    .J(or_1_out), .clk(CLK), .K(or_1_out), .Q(Q3), .Qn(j_k_ff_4_qn), .reset(not_1_out));  // open: preset, en
  Hex_Digit_Display hex_digit_display_1 (.value({Q3, Q2, Q1, Q0}));  // open: dp

  // Notes on the sheet:
  //   MOD 9 COUNTER
endmodule

module mod6 (
  input  VCC,
  input  CLK,
  input  CLR,
  output Q1,
  output Q2,
  output Q0
);

  wire and_1_out, and_2_out, not_1_out, or_1_out;

  J_K_Flip_Flop j_k_ff_1 (.J(VCC), .clk(CLK), .K(VCC), .Q(Q0), .reset(or_1_out));  // open: Qn, preset, en
  or or_1 (or_1_out, and_1_out, not_1_out);
  J_K_Flip_Flop j_k_ff_2 (.J(Q0), .clk(CLK), .K(Q0), .Q(Q1), .reset(or_1_out));  // open: Qn, preset, en
  and and_1 (and_1_out, Q1, Q2);
  not not_1 (not_1_out, CLR);
  and and_2 (and_2_out, Q0, Q1);
  J_K_Flip_Flop j_k_ff_3 (.J(and_2_out), .clk(CLK), .K(and_2_out), .Q(Q2), .reset(or_1_out));  // open: Qn, preset, en
  Hex_Digit_Display hex_digit_display_1 (.value({1'b0, Q2, Q1, Q0}));  // open: dp

  // Notes on the sheet:
  //   MOD 6 COUNTER
endmodule

module _7_seg_driver (
  input  EN_prime,
  input  Q0,
  input  Q1,
  input  Q2,
  input  Q3,
  output NXT,
  output A,
  output B,
  output C,
  output D,
  output E,
  output F,
  output G
);

  wire and_1_out, and_2_out, and_3_out, and_4_out, and_5_out, and_6_out, and_7_out, and_8_out, and_9_out,
       and_10_out, and_11_out, and_12_out, and_13_out, and_14_out, and_15_out, and_16_out, and_17_out,
       not_1_out, not_2_out, not_3_out, not_4_out, not_5_out, not_6_out, not_7_out, not_8_out, not_9_out,
       not_10_out, not_11_out, or_1_out, or_2_out, or_3_out, or_4_out, or_5_out, or_6_out, or_7_out;

  not not_1 (not_1_out, EN_prime);
  not not_2 (not_2_out, Q1);
  not not_3 (not_3_out, Q3);
  not not_4 (not_4_out, Q0);
  not not_5 (not_5_out, Q2);
  not not_6 (not_6_out, Q0);
  not not_7 (not_7_out, Q2);
  and and_1 (and_1_out, Q1, Q0);
  and and_2 (and_2_out, not_2_out, not_4_out);
  not not_8 (not_8_out, Q3);
  not not_9 (not_9_out, Q0);
  and and_3 (and_3_out, not_6_out, not_7_out);
  and and_4 (and_4_out, Q0, Q2);
  and and_5 (and_5_out, Q0, not_3_out);
  and and_6 (and_6_out, not_3_out, not_2_out);
  not not_10 (not_10_out, Q1);
  or or_1 (or_1_out, and_1_out, and_2_out, not_5_out, Q3);
  or or_2 (or_2_out, and_5_out, and_6_out, Q2, Q3);
  not not_11 (not_11_out, Q2);
  or or_3 (or_3_out, Q1, Q3, and_3_out, and_4_out);
  or or_4 (or_4_out, Q1, Q3, Q2);
  and and_7 (and_7_out, Q2, not_10_out, Q0);
  and and_8 (and_8_out, not_9_out, Q2, Q1);
  and and_9 (and_9_out, not_9_out, not_10_out);
  and and_10 (and_10_out, not_9_out, not_10_out, not_5_out);
  and and_11 (and_11_out, not_9_out, Q3);
  and and_12 (and_12_out, not_9_out, Q1);
  and and_13 (and_13_out, not_10_out, Q2, Q0);
  and and_14 (and_14_out, not_11_out, Q1);
  and and_15 (and_15_out, not_9_out, Q3);
  and and_16 (and_16_out, not_9_out, Q1);
  and and_17 (and_17_out, not_9_out, not_11_out, not_8_out);
  nand nand_1 (NXT, Q0, Q3);
  or or_5 (or_5_out, Q3, and_7_out, and_8_out, and_9_out);
  or or_6 (or_6_out, and_10_out, and_11_out, and_12_out, and_13_out, and_14_out);
  or or_7 (or_7_out, and_15_out, and_16_out, and_17_out);
  _7_Segment_Display u_7_segment_display_1 (
    .g(or_4_out), .f(or_5_out), .a(or_3_out), .b(or_1_out), .e(or_7_out), .d(or_6_out), .c(or_2_out));  // open: dp
  and and_18 (A, not_1_out, or_3_out);
  and and_19 (B, not_1_out, or_1_out);
  and and_20 (C, not_1_out, or_2_out);
  and and_21 (D, not_1_out, or_6_out);
  and and_22 (E, not_1_out, or_7_out);
  and and_23 (F, not_1_out, or_5_out);
  and and_24 (G, not_1_out, or_4_out);

  // Notes on the sheet:
  //   B
  //   A
  //   C
  //   F
  //   D
  //   E
  //   G
  //   7 SEGMENT DISPLAY DRIVER FOR MOD 9
endmodule

module _7_seg_driver_mod6 (
  input  EN_prime,
  input  Q0,
  input  Q1,
  input  Q2,
  input  Q3,
  output NXT,
  output A,
  output B,
  output C,
  output D,
  output E,
  output F,
  output G
);

  wire and_1_out, and_2_out, and_3_out, and_4_out, and_5_out, and_6_out, and_7_out, and_8_out, and_9_out,
       and_10_out, and_11_out, and_12_out, and_13_out, and_14_out, and_15_out, and_16_out, and_17_out,
       not_1_out, not_2_out, not_3_out, not_4_out, not_5_out, not_6_out, not_7_out, not_8_out, not_9_out,
       not_10_out, not_11_out, or_1_out, or_2_out, or_3_out, or_4_out, or_5_out, or_6_out, or_7_out;

  not not_1 (not_1_out, EN_prime);
  not not_2 (not_2_out, Q1);
  not not_3 (not_3_out, Q3);
  not not_4 (not_4_out, Q0);
  not not_5 (not_5_out, Q2);
  not not_6 (not_6_out, Q0);
  not not_7 (not_7_out, Q2);
  and and_1 (and_1_out, Q1, Q0);
  and and_2 (and_2_out, not_2_out, not_4_out);
  not not_8 (not_8_out, Q3);
  not not_9 (not_9_out, Q0);
  and and_3 (and_3_out, not_6_out, not_7_out);
  and and_4 (and_4_out, Q0, Q2);
  and and_5 (and_5_out, Q0, not_3_out);
  and and_6 (and_6_out, not_3_out, not_2_out);
  not not_10 (not_10_out, Q1);
  or or_1 (or_1_out, and_1_out, and_2_out, not_5_out, Q3);
  or or_2 (or_2_out, and_5_out, and_6_out, Q2, Q3);
  not not_11 (not_11_out, Q2);
  or or_3 (or_3_out, Q1, Q3, and_3_out, and_4_out);
  or or_4 (or_4_out, Q1, Q3, Q2);
  and and_7 (and_7_out, Q2, not_10_out, Q0);
  and and_8 (and_8_out, not_9_out, Q2, Q1);
  and and_9 (and_9_out, not_9_out, not_10_out);
  and and_10 (and_10_out, not_9_out, not_10_out, not_5_out);
  and and_11 (and_11_out, not_9_out, Q3);
  and and_12 (and_12_out, not_9_out, Q1);
  and and_13 (and_13_out, not_10_out, Q2, Q0);
  and and_14 (and_14_out, not_11_out, Q1);
  and and_15 (and_15_out, not_9_out, Q3);
  and and_16 (and_16_out, not_9_out, Q1);
  and and_17 (and_17_out, not_9_out, not_11_out, not_8_out);
  nand nand_1 (NXT, Q2, Q1);
  or or_5 (or_5_out, Q3, and_7_out, and_8_out, and_9_out);
  or or_6 (or_6_out, and_10_out, and_11_out, and_12_out, and_13_out, and_14_out);
  or or_7 (or_7_out, and_15_out, and_16_out, and_17_out);
  _7_Segment_Display u_7_segment_display_1 (
    .g(or_4_out), .f(or_5_out), .a(or_3_out), .b(or_1_out), .e(or_7_out), .d(or_6_out), .c(or_2_out));  // open: dp
  and and_18 (A, not_1_out, or_3_out);
  and and_19 (B, not_1_out, or_1_out);
  and and_20 (C, not_1_out, or_2_out);
  and and_21 (D, not_1_out, or_6_out);
  and and_22 (E, not_1_out, or_7_out);
  and and_23 (F, not_1_out, or_5_out);
  and and_24 (G, not_1_out, or_4_out);

  // Notes on the sheet:
  //   B
  //   A
  //   C
  //   F
  //   D
  //   E
  //   G
  //   7 SEGMENT DISPLAY DRIVER FOR MOD 6
endmodule

module mod3 (
  input  VCC,
  input  CLK,
  input  CLR,
  output Q1,
  output Q0
);

  wire and_1_out, not_1_out, or_1_out;

  J_K_Flip_Flop j_k_ff_1 (.J(VCC), .clk(CLK), .K(VCC), .Q(Q0), .reset(or_1_out));  // open: Qn, preset, en
  or or_1 (or_1_out, and_1_out, not_1_out);
  and and_1 (and_1_out, Q1, Q0);
  J_K_Flip_Flop j_k_ff_2 (.J(Q0), .clk(CLK), .K(Q0), .Q(Q1), .reset(or_1_out));  // open: Qn, preset, en
  not not_1 (not_1_out, CLR);
  Hex_Digit_Display hex_digit_display_1 (.value({2'b00, Q1, Q0}));  // open: dp

  // Notes on the sheet:
  //   MOD 3 COUNTER
endmodule
