// Logisim project IC-24HRCLOCK.circ as structural Verilog
module main (
  input  SET_MINUTES,
  input  SET_SECONDS,
  input  SET_HOUR,
  input  STOP
);

  wire clock_1_out, decade_counter_1_nxt, decade_counter_1_q0, decade_counter_1_q1, decade_counter_1_q3,
       decade_counter_2_nxt, decade_counter_2_q0, decade_counter_2_q1, decade_counter_2_q2,
       decade_counter_2_q3, decade_counter_3_nxt, decade_counter_3_q0, decade_counter_3_q1,
       decade_counter_3_q2, decade_counter_3_q3, mod6_1_q0, mod6_1_q2, mod6_2_nxt, mod6_2_q0, mod6_2_q1,
       mod6_2_q2, mod6_3_q0, mod6_3_q1, mod6_3_q2, n7400_1_p3, n7400_1_p4, n7400_1_p5, n7408_1_p1,
       n7408_1_p3, n7432_1_p3, n7448_1_p9, n7448_1_p10, n7448_1_p11, n7448_1_p12, n7448_1_p13, n7448_1_p14,
       n7448_1_p15, n7448_2_p9, n7448_2_p10, n7448_2_p11, n7448_2_p12, n7448_2_p13, n7448_2_p14, n7448_2_p15,
       n7448_3_p9, n7448_3_p10, n7448_3_p11, n7448_3_p12, n7448_3_p13, n7448_3_p14, n7448_3_p15, n7448_4_p9,
       n7448_4_p10, n7448_4_p11, n7448_4_p12, n7448_4_p13, n7448_4_p14, n7448_4_p15, n7448_5_p9, n7448_5_p10,
       n7448_5_p11, n7448_5_p12, n7448_5_p13, n7448_5_p14, n7448_5_p15, n7448_6_p9, n7448_6_p10, n7448_6_p11,
       n7448_6_p12, n7448_6_p13, n7448_6_p14, n7448_6_p15, n7486_1_p3, n7486_1_p7, n7486_1_p8;

  Clock clock_1 (.out(clock_1_out));
  // _7408 7408_1: pin names not known; wires that end beside it: n7408_1_p1, clock_1_out, n7408_1_p3
  // _7404 7404_1: pin names not known; wires that end beside it: STOP, n7408_1_p1
  // _7400 7400_1: pin names not known; wires that end beside it: 1'b0, 1'b1, n7400_1_p3, n7400_1_p4, n7400_1_p5
  mod6 mod6_1 (
    .CLK(decade_counter_1_nxt), .VCC(1'b1), .GND(1'b0), .Q0(mod6_1_q0), .Q1(n7400_1_p4), .Q2(mod6_1_q2),
    .CLR(n7400_1_p5));  // open: NXT
  // _7448 7448_1: pin names not known; wires that end beside it: n7400_1_p4, mod6_1_q2, 1'b1, 1'b1, 1'b0, mod6_1_q0, 1'b0, 1'b1, n7448_1_p9, n7448_1_p10, n7448_1_p11, n7448_1_p12, n7448_1_p13, n7448_1_p14, n7448_1_p15
  _7_Segment_Display u_7_segment_display_1 (
    .g(n7448_1_p10), .f(n7448_1_p9), .a(n7448_1_p11), .b(n7448_1_p12), .e(n7448_1_p15), .d(n7448_1_p14),
    .c(n7448_1_p13));  // open: dp
  decade_counter decade_counter_1 (
    .NXT(decade_counter_1_nxt), .CLK(n7486_1_p3), .VCC(1'b1), .CLR(n7400_1_p5), .GND(1'b0),
    .Q0(decade_counter_1_q0), .Q1(decade_counter_1_q1), .Q2(n7400_1_p3), .Q3(decade_counter_1_q3));
  // _7448 7448_2: pin names not known; wires that end beside it: decade_counter_1_q1, n7400_1_p3, 1'b1, 1'b1, decade_counter_1_q3, decade_counter_1_q0, 1'b0, 1'b1, n7448_2_p9, n7448_2_p10, n7448_2_p11, n7448_2_p12, n7448_2_p13, n7448_2_p14, n7448_2_p15
  _7_Segment_Display u_7_segment_display_2 (
    .g(n7448_2_p10), .f(n7448_2_p9), .a(n7448_2_p11), .b(n7448_2_p12), .e(n7448_2_p15), .d(n7448_2_p14),
    .c(n7448_2_p13));  // open: dp
  mod6 mod6_2 (
    .CLK(decade_counter_2_nxt), .VCC(1'b1), .GND(1'b0), .Q0(mod6_2_q0), .Q1(mod6_2_q1), .Q2(mod6_2_q2),
    .NXT(mod6_2_nxt), .CLR(n7400_1_p5));
  LED led_1 (.in(1'b1));
  LED led_2 (.in(1'b1));
  // _7486 7486_1: pin names not known; wires that end beside it: mod6_2_nxt, SET_HOUR, n7486_1_p3, 1'b0, 1'b1, SET_MINUTES, n7486_1_p7, n7486_1_p8
  // _7448 7448_3: pin names not known; wires that end beside it: mod6_2_q1, mod6_2_q2, 1'b1, 1'b1, 1'b0, mod6_2_q0, 1'b0, 1'b1, n7448_3_p9, n7448_3_p10, n7448_3_p11, n7448_3_p12, n7448_3_p13, n7448_3_p14, n7448_3_p15
  _7_Segment_Display u_7_segment_display_3 (
    .g(n7448_3_p10), .f(n7448_3_p9), .a(n7448_3_p11), .b(n7448_3_p12), .e(n7448_3_p15), .d(n7448_3_p14),
    .c(n7448_3_p13));  // open: dp
  decade_counter decade_counter_2 (
    .NXT(decade_counter_2_nxt), .CLK(n7486_1_p8), .VCC(1'b1), .CLR(n7400_1_p5), .GND(1'b0),
    .Q0(decade_counter_2_q0), .Q1(decade_counter_2_q1), .Q2(decade_counter_2_q2), .Q3(decade_counter_2_q3));
  // _7448 7448_4: pin names not known; wires that end beside it: decade_counter_2_q1, decade_counter_2_q2, 1'b1, 1'b1, decade_counter_2_q3, decade_counter_2_q0, 1'b0, 1'b1, n7448_4_p9, n7448_4_p10, n7448_4_p11, n7448_4_p12, n7448_4_p13, n7448_4_p14, n7448_4_p15
  _7_Segment_Display u_7_segment_display_4 (
    .g(n7448_4_p10), .f(n7448_4_p9), .a(n7448_4_p11), .b(n7448_4_p12), .e(n7448_4_p15), .d(n7448_4_p14),
    .c(n7448_4_p13));  // open: dp
  mod6 mod6_3 (
    .CLK(decade_counter_3_nxt), .VCC(1'b1), .GND(1'b0), .Q0(mod6_3_q0), .Q1(mod6_3_q1), .Q2(mod6_3_q2),
    .NXT(n7486_1_p7), .CLR(n7400_1_p5));
  LED led_3 (.in(1'b1));
  LED led_4 (.in(1'b1));
  // _7448 7448_5: pin names not known; wires that end beside it: mod6_3_q1, mod6_3_q2, 1'b1, 1'b1, 1'b0, mod6_3_q0, 1'b0, 1'b1, n7448_5_p9, n7448_5_p10, n7448_5_p11, n7448_5_p12, n7448_5_p13, n7448_5_p14, n7448_5_p15
  _7_Segment_Display u_7_segment_display_5 (
    .g(n7448_5_p10), .f(n7448_5_p9), .a(n7448_5_p11), .b(n7448_5_p12), .e(n7448_5_p15), .d(n7448_5_p14),
    .c(n7448_5_p13));  // open: dp
  // _7432 7432_1: pin names not known; wires that end beside it: SET_SECONDS, n7408_1_p3, n7432_1_p3
  decade_counter decade_counter_3 (
    .NXT(decade_counter_3_nxt), .CLK(n7432_1_p3), .VCC(1'b1), .CLR(n7400_1_p5), .GND(1'b0),
    .Q0(decade_counter_3_q0), .Q1(decade_counter_3_q1), .Q2(decade_counter_3_q2), .Q3(decade_counter_3_q3));
  // _7448 7448_6: pin names not known; wires that end beside it: decade_counter_3_q1, decade_counter_3_q2, 1'b1, 1'b1, decade_counter_3_q3, decade_counter_3_q0, 1'b0, 1'b1, n7448_6_p9, n7448_6_p10, n7448_6_p11, n7448_6_p12, n7448_6_p13, n7448_6_p14, n7448_6_p15
  _7_Segment_Display u_7_segment_display_6 (
    .g(n7448_6_p10), .f(n7448_6_p9), .a(n7448_6_p11), .b(n7448_6_p12), .e(n7448_6_p15), .d(n7448_6_p14),
    .c(n7448_6_p13));  // open: dp
endmodule

module decade_counter (
  input  CLK,
  input  VCC,
  input  CLR,
  input  GND,
  output NXT,
  output Q0,
  output Q1,
  output Q2,
  output Q3
);

  wire n7408_1_p1, n7408_1_p6, n7408_1_p11, n7408_1_p14, n7476_1_p2, n7476_1_p10, n7476_2_p9;

  LED led_1 (.in(Q3));
  LED led_2 (.in(Q2));
  LED led_3 (.in(Q1));
  LED led_4 (.in(Q0));
  // _7476 7476_1: pin names not known; wires that end beside it: CLK, n7476_1_p2, VCC, VCC, CLK, n7476_1_p2, VCC, Q0, GND, n7476_1_p10, Q1, n7476_1_p10
  // _7408 7408_1: pin names not known; wires that end beside it: n7408_1_p1, Q0, n7476_1_p10, Q0, Q1, n7408_1_p6, GND, VCC, Q2, n7408_1_p6, n7408_1_p11, Q0, Q3, n7408_1_p14
  // _7476 7476_2: pin names not known; wires that end beside it: CLK, n7476_1_p2, n7408_1_p6, VCC, CLK, n7408_1_p6, Q2, GND, n7476_2_p9, Q3, n7408_1_p1, n7476_2_p9
  // _7432 7432_1: pin names not known; wires that end beside it: n7408_1_p11, n7408_1_p14, n7476_2_p9, GND, VCC, n7476_1_p2
  // _7400 7400_1: pin names not known; wires that end beside it: Q3, Q0, NXT
  // _7404 7404_1: pin names not known; wires that end beside it: CLR, n7476_1_p2
endmodule

module mod6 (
  input  CLK,
  input  VCC,
  input  CLR,
  input  GND,
  output Q0,
  output Q1,
  output Q2,
  output NXT
);

  wire n7408_1_p3, n7408_1_p8, n7432_1_p3, n7432_1_p6, n7476_1_p2;

  Hex_Digit_Display hex_digit_display_1 (.value({1'b0, Q2, Q1, Q0}));  // open: dp
  // _7476 7476_1: pin names not known; wires that end beside it: CLK, n7476_1_p2, VCC, VCC, CLK, n7476_1_p2, VCC, Q0, GND, Q0, Q1, Q0
  // _7408 7408_1: pin names not known; wires that end beside it: Q0, Q1, n7408_1_p3, GND, VCC, Q2, Q1, n7408_1_p8
  // _7432 7432_1: pin names not known; wires that end beside it: GND, VCC, n7432_1_p3, n7432_1_p3, n7408_1_p8, n7432_1_p6, n7476_1_p2
  // _7476 7476_2: pin names not known; wires that end beside it: CLK, n7476_1_p2, n7408_1_p3, VCC, n7408_1_p3, Q2, GND
  // _7404 7404_1: pin names not known; wires that end beside it: CLR, n7432_1_p6, GND, VCC
  // _7400 7400_1: pin names not known; wires that end beside it: Q2, Q0, NXT
endmodule
